# Fritzing sketch Pico_watering_RGB (saved by Fritzing 0.9.9b)
circuit board: 8.46667cm x 5.64444cm
breadboards: 1

parts:
  Mod1 = Raspberry Pi Pico
  BAT2 = Battery Holders [package=battery-aa-kit]
  BAT3 = Battery Holders [package=battery-aa-kit]
  BAT4 = Battery Holders [package=battery-aa-kit]
  Part1 = Adafruit DRV8833 DC/Stepper Motor Driver [part_number="Adafruit #3297"]
  BAT1 = Battery Holders [package=battery-aa]
  WATER_PUMP1 = gear-motor
  부품3 = FC-28 Soil Hygrometer Module - Probe
  부품4 = FC-28 Soil Hygrometer Module
  LED3 = RGB LED (com. cathode, rgb) [package="5 mm [THT]"]

nets:
  GND: Mod1.pin_3, Mod1.pin_8, Mod1.pin_13, Mod1.pin_18, Mod1.pin_23, Mod1.pin_28, Mod1.pin_33, Mod1.pin_38, Mod1.pin_42, BAT2.-, BAT3.+, BAT4.-, Part1.GND, BAT1.+, 부품4.GND, LED3.green_anode
  N1: Mod1.pin_6, LED3.blue_anode
  N2: Mod1.pin_9, LED3.common_cathode
  N3: Mod1.pin_10, LED3.red_anode
  N4: Mod1.pin_19, Part1.AIN1
  N5: Mod1.pin_20, Part1.AIN2
  N6: Mod1.pin_31, 부품4.AO
  N7: Mod1.pin_34, 부품4.VCC
  N8: Mod1.pin_39, BAT2.+, BAT3.-, BAT4.+, Part1.VMOTOR, BAT1.-
  N9: Part1.AOUT2, WATER_PUMP1.pin_2
  N10: Part1.AOUT1, WATER_PUMP1.pin_1
  N11: 부품3.POS, 부품4.POS
  N12: 부품3.NEG, 부품4.NEG

custom parts:
  Raspberry Pi Pico: Raspberry Pi Pico. Based around the RP2040 microcontroller the Pico is a low cost microcontroller device bringing Raspberry Pi quality, cost, and easy of use to the microcontroller space. Jan 2021, Split part in to two versions: tht (this one) and SMD. This one will drill holes for a .1 in header in pcb to allow plugging in the module as well as providing pads to solder the module to the top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
  Adafruit DRV8833 DC/Stepper Motor Driver: Spin two DC motors or step one bi-polar or uni-polar stepper with up to 1.2A per channel using the DRV8833. This motor driver chip is a nice alternative to the TB6612 driver. Like that chip, you get 2 full H-bridges, but this chip is better for low voltage uses (can run from 2.7V up to 10.8V motor power) and has built in current limiting capability. We set it up for 1A current limiting so you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
  FC-28 Soil Hygrometer Module - Probe: The FC-28 is a soil hygrometer module that uses the Texas Instruments LM393 comparator chip to provide an analog measurement of soil humidity.
  FC-28 Soil Hygrometer Module: The FC-28 is a soil hygrometer module that uses the Texas Instruments LM393 comparator chip to provide an analog measurement of soil humidity. The digital output is high when soil moisture is over a certain threshold, as determined by adjusting the potentiometer.
